# Fritzing sketch robotikaFritzing_bb (saved by Fritzing 0.9.9b)
breadboards: 1

parts:
  U1 = ESP8266 NodeMCU LoLin module
  Part1 = Arduino Micro (Rev3)
  M1 = gear-motor
  IC1 = L293D [package=THT]
  J1 = Piezo Speaker
  J2 = Basic Servo
  LED1 = smd LED [color="White (4500K)" package="0603 [SMD]"]
  R1 = Resistor [tolerance=±5% resistance=220 package="0603 [SMD]"]
  HC-SR04_Sensor_1 = HC-SR04 Ultrasonic Distance Sensor
  LED2 = smd LED [color="Red (633nm)" package="0603 [SMD]"]
  LED3 = smd LED [color="Red (633nm)" package="0603 [SMD]"]
  LED4 = smd LED [color="Red (633nm)" package="0603 [SMD]"]
  LED5 = smd LED [color="Red (633nm)" package="0603 [SMD]"]
  R2 = Resistor [tolerance=±5% resistance=220 package="0603 [SMD]"]

nets:
  GND: U1.GND, Part1.GND, J1.pin1, J2.gnd, R1.Pin_1, HC-SR04_Sensor_1.GND, R2.Pin_0
  N1: U1.RX, Part1.D1/TX
  N2: U1.TX, Part1.D0/RX
  VCC: U1.Vin, Part1.5V, IC1.+V, J2.vcc, HC-SR04_Sensor_1.VCC
  N3: Part1.D2/SDA, LED2.anode, LED3.anode, LED4.anode, LED5.anode
  N4: Part1.D3/SCL, IC1.Enable_1
  N5: Part1.D4_PWM/A6, IC1.In_1
  N6: Part1.D5_PWM, J1.pin2
  N7: Part1.D6_PWM/A7, J2.pulse
  N8: Part1.D7, IC1.In_2
  N9: Part1.D8_PWM/A8, LED1.anode
  N10: Part1.D9_PWM/A9, HC-SR04_Sensor_1.ECHO
  N11: Part1.D10_PWM/A10, HC-SR04_Sensor_1.TRIG
  N12: M1.pin_1, IC1.Out_2_(_Controlled_by_Enable_1_)
  N13: M1.pin_2, IC1.Out_1_(_Controlled_by_Enable_1_)
  N14: LED1.cathode, R1.Pin_0
  N15: LED2.cathode, LED3.cathode, LED4.cathode, LED5.cathode, R2.Pin_1

custom parts:
  ESP8266 NodeMCU LoLin module: ESP8266 based NodeMCU
